// Logisim project 8_bit_adder.circ as structural Verilog: 1 circuit, main circuit main
module main (
  input  A,
  input  A_2,
  input  A_3,
  input  A_4,
  input  A_5,
  input  A_6,
  input  A_7,
  input  A_8,
  input  B,
  input  B_2,
  input  B_3,
  input  B_4,
  input  B_5,
  input  B_6,
  input  B_7,
  input  B_8,
  input  CARRY_IN,
  output SUM,
  output SUM_2,
  output SUM_3,
  output SUM_4,
  output SUM_5,
  output SUM_6,
  output SUM_7,
  output SUM_8,
  output CARRY_OUT_OVERFLOW
);

  wire and_1_out, and_2_out, and_3_out, and_4_out, and_5_out, and_6_out, and_7_out, and_8_out, and_9_out,
       and_10_out, and_11_out, and_12_out, and_13_out, and_14_out, and_15_out, and_16_out, and_17_out,
       and_18_out, and_19_out, and_20_out, and_21_out, and_22_out, and_23_out, and_24_out, and_25_out,
       and_26_out, and_27_out, and_28_out, and_29_out, and_30_out, and_31_out, and_32_out, and_33_out,
       and_34_out, and_35_out, and_36_out, and_37_out, and_38_out, and_39_out, and_40_out, and_41_out,
       and_42_out, and_43_out, and_44_out, and_45_out, and_46_out, and_47_out, and_48_out, and_49_out,
       and_50_out, and_51_out, and_52_out, and_53_out, and_54_out, and_55_out, and_56_out, not_1_out,
       not_2_out, not_3_out, not_4_out, not_5_out, not_6_out, not_7_out, not_8_out, not_9_out, not_10_out,
       not_11_out, not_12_out, not_13_out, not_14_out, not_15_out, not_16_out, not_17_out, not_18_out,
       not_19_out, not_20_out, not_21_out, not_22_out, not_23_out, not_24_out, or_4_out, or_6_out, or_8_out,
       or_10_out, or_12_out, or_14_out, or_16_out;

  not not_1 (not_1_out, A);
  not not_2 (not_2_out, B);
  not not_3 (not_3_out, or_4_out);
  and and_1 (and_1_out, not_1_out, not_2_out, or_4_out);
  and and_2 (and_2_out, not_1_out, B, not_3_out);
  and and_3 (and_3_out, A, not_2_out, not_3_out);
  and and_4 (and_4_out, A, B, or_4_out);
  and and_5 (and_5_out, not_1_out, B, or_4_out);
  and and_6 (and_6_out, A, not_2_out, or_4_out);
  and and_7 (and_7_out, A, B, not_3_out);
  or or_1 (SUM, and_1_out, and_2_out, and_3_out, and_4_out);
  or or_2 (CARRY_OUT_OVERFLOW, and_5_out, and_6_out, and_7_out, and_4_out);
  not not_4 (not_4_out, A_2);
  not not_5 (not_5_out, B_2);
  not not_6 (not_6_out, or_6_out);
  and and_8 (and_8_out, not_4_out, not_5_out, or_6_out);
  and and_9 (and_9_out, not_4_out, B_2, not_6_out);
  and and_10 (and_10_out, A_2, not_5_out, not_6_out);
  and and_11 (and_11_out, A_2, B_2, or_6_out);
  and and_12 (and_12_out, not_4_out, B_2, or_6_out);
  and and_13 (and_13_out, A_2, not_5_out, or_6_out);
  and and_14 (and_14_out, A_2, B_2, not_6_out);
  or or_3 (SUM_2, and_8_out, and_9_out, and_10_out, and_11_out);
  or or_4 (or_4_out, and_12_out, and_13_out, and_14_out, and_11_out);
  not not_7 (not_7_out, A_3);
  not not_8 (not_8_out, B_3);
  not not_9 (not_9_out, or_8_out);
  and and_15 (and_15_out, not_7_out, not_8_out, or_8_out);
  and and_16 (and_16_out, not_7_out, B_3, not_9_out);
  and and_17 (and_17_out, A_3, not_8_out, not_9_out);
  and and_18 (and_18_out, A_3, B_3, or_8_out);
  and and_19 (and_19_out, not_7_out, B_3, or_8_out);
  and and_20 (and_20_out, A_3, not_8_out, or_8_out);
  and and_21 (and_21_out, A_3, B_3, not_9_out);
  or or_5 (SUM_3, and_15_out, and_16_out, and_17_out, and_18_out);
  or or_6 (or_6_out, and_19_out, and_20_out, and_21_out, and_18_out);
  not not_10 (not_10_out, A_4);
  not not_11 (not_11_out, B_4);
  not not_12 (not_12_out, or_10_out);
  and and_22 (and_22_out, not_10_out, not_11_out, or_10_out);
  and and_23 (and_23_out, not_10_out, B_4, not_12_out);
  and and_24 (and_24_out, A_4, not_11_out, not_12_out);
  and and_25 (and_25_out, A_4, B_4, or_10_out);
  and and_26 (and_26_out, not_10_out, B_4, or_10_out);
  and and_27 (and_27_out, A_4, not_11_out, or_10_out);
  and and_28 (and_28_out, A_4, B_4, not_12_out);
  or or_7 (SUM_4, and_22_out, and_23_out, and_24_out, and_25_out);
  or or_8 (or_8_out, and_26_out, and_27_out, and_28_out, and_25_out);
  not not_13 (not_13_out, A_5);
  not not_14 (not_14_out, B_5);
  not not_15 (not_15_out, or_12_out);
  and and_29 (and_29_out, not_13_out, not_14_out, or_12_out);
  and and_30 (and_30_out, not_13_out, B_5, not_15_out);
  and and_31 (and_31_out, A_5, not_14_out, not_15_out);
  and and_32 (and_32_out, A_5, B_5, or_12_out);
  and and_33 (and_33_out, not_13_out, B_5, or_12_out);
  and and_34 (and_34_out, A_5, not_14_out, or_12_out);
  and and_35 (and_35_out, A_5, B_5, not_15_out);
  or or_9 (SUM_5, and_29_out, and_30_out, and_31_out, and_32_out);
  or or_10 (or_10_out, and_33_out, and_34_out, and_35_out, and_32_out);
  not not_16 (not_16_out, A_6);
  not not_17 (not_17_out, B_6);
  not not_18 (not_18_out, or_14_out);
  and and_36 (and_36_out, not_16_out, not_17_out, or_14_out);
  and and_37 (and_37_out, not_16_out, B_6, not_18_out);
  and and_38 (and_38_out, A_6, not_17_out, not_18_out);
  and and_39 (and_39_out, A_6, B_6, or_14_out);
  and and_40 (and_40_out, not_16_out, B_6, or_14_out);
  and and_41 (and_41_out, A_6, not_17_out, or_14_out);
  and and_42 (and_42_out, A_6, B_6, not_18_out);
  or or_11 (SUM_6, and_36_out, and_37_out, and_38_out, and_39_out);
  or or_12 (or_12_out, and_40_out, and_41_out, and_42_out, and_39_out);
  not not_19 (not_19_out, A_7);
  not not_20 (not_20_out, B_7);
  not not_21 (not_21_out, or_16_out);
  and and_43 (and_43_out, not_19_out, not_20_out, or_16_out);
  and and_44 (and_44_out, not_19_out, B_7, not_21_out);
  and and_45 (and_45_out, A_7, not_20_out, not_21_out);
  and and_46 (and_46_out, A_7, B_7, or_16_out);
  and and_47 (and_47_out, not_19_out, B_7, or_16_out);
  and and_48 (and_48_out, A_7, not_20_out, or_16_out);
  and and_49 (and_49_out, A_7, B_7, not_21_out);
  or or_13 (SUM_7, and_43_out, and_44_out, and_45_out, and_46_out);
  or or_14 (or_14_out, and_47_out, and_48_out, and_49_out, and_46_out);
  not not_22 (not_22_out, A_8);
  not not_23 (not_23_out, B_8);
  not not_24 (not_24_out, CARRY_IN);
  and and_50 (and_50_out, not_22_out, not_23_out, CARRY_IN);
  and and_51 (and_51_out, not_22_out, B_8, not_24_out);
  and and_52 (and_52_out, A_8, not_23_out, not_24_out);
  and and_53 (and_53_out, A_8, B_8, CARRY_IN);
  and and_54 (and_54_out, not_22_out, B_8, CARRY_IN);
  and and_55 (and_55_out, A_8, not_23_out, CARRY_IN);
  and and_56 (and_56_out, A_8, B_8, not_24_out);
  or or_15 (SUM_8, and_50_out, and_51_out, and_52_out, and_53_out);
  or or_16 (or_16_out, and_54_out, and_55_out, and_56_out, and_53_out);
endmodule
