// Logisim project full_adder.circ as structural Verilog: 1 circuit, main circuit main
module main (
  input  A,
  input  B,
  input  CARRY_IN,
  output SUM,
  output CARRY_OUT
);

  wire and_1_out, and_2_out, and_3_out, and_4_out, and_5_out, and_6_out, and_7_out, not_1_out, not_2_out,
       not_3_out;

  not not_1 (not_1_out, A);
  not not_2 (not_2_out, B);
  not not_3 (not_3_out, CARRY_IN);
  and and_1 (and_1_out, not_1_out, not_2_out, CARRY_IN);
  and and_2 (and_2_out, not_1_out, B, not_3_out);
  and and_3 (and_3_out, A, not_2_out, not_3_out);
  and and_4 (and_4_out, A, B, CARRY_IN);
  and and_5 (and_5_out, not_1_out, B, CARRY_IN);
  and and_6 (and_6_out, A, not_2_out, CARRY_IN);
  and and_7 (and_7_out, A, B, not_3_out);
  or or_1 (SUM, and_1_out, and_2_out, and_3_out, and_4_out);
  or or_2 (CARRY_OUT, and_5_out, and_6_out, and_7_out, and_4_out);
endmodule
